# Fritzing sketch dewo_radio_si4703_pcb_v2 (saved by Fritzing 0.9.3b)
circuit board: 8.5cm x 5cm
breadboards: 1

parts:
  Nano = Arduino Nano (Rev3.0)
  U1 = Voltage Regulator - 5V [package="TO220 [THT]"]
  J1 = Screw terminal - 2 pins [package=THT]
  C1 = Electrolytic Capacitor [capacitance=47µF voltage=16V package="100 mil [THT, electrolytic]"]
  C2 = Electrolytic Capacitor [capacitance=47µF voltage=16V package="100 mil [THT, electrolytic]"]
  C3 = Ceramic Capacitor [capacitance=100nF package="100 mil [THT, multilayer]"]
  LCD_I2C = female pin header, 4 pins [form="♀ (female)"]
  Si4703 = Digital FM Radio Receiver
  Si4703_OUT = female pin header, 5 pins [form="♀ (female)"]
  Rotary_Encoder = female pin header, 5 pins [form="♀ (female)"]
  PAM_INPUT = female pin header, 7 pins [form="♀ (female)"]
  PAM_OUTPUT = female pin header, 7 pins [form="♀ (female)"]
  D1 = Rectifier Diode [part_number=1N4004 package="300 mil [THT]"]
  R1 = Resistor [tolerance=±5% resistance=10k package=THT]
  SPEAKER = Screw terminal - 2 pins [package=THT]
  R3 = Resistor [tolerance=±5% resistance=10k package=THT]
  J5 = female pin header, 1 pin [form="♀ (female)"]
  DS3231 = female pin header, 4 pins [form="♀ (female)"]
  R4 = Resistor [tolerance=±5% resistance=10k package=THT]
  J7 = female pin header, 6 pins [form="♀ (female)"]  # not connected
  J8 = female pin header, 1 pin [form="♀ (female)"]

nets:
  GND: Nano.GND, U1.GND, J1.pin2, C1.-, C2.-, C3.0, LCD_I2C.pin1, Si4703.GND, Rotary_Encoder.pin5, PAM_INPUT.pin2, PAM_INPUT.pin7, J5.pin1, DS3231.pin4, J8.pin1
  Reset: Nano.D2, Si4703.!RST
  N1: Nano.VIN, U1.output_voltage, C2.+, C3.1, LCD_I2C.pin2, Rotary_Encoder.pin4, PAM_INPUT.pin6, R3.Pin_0
  N2: Nano.A5, LCD_I2C.pin4, Si4703.SCLK, DS3231.pin1
  N3: Nano.A4, LCD_I2C.pin3, Si4703.SDIO, DS3231.pin2
  N4: Nano.A2, Rotary_Encoder.pin1
  N5: Nano.A1, Rotary_Encoder.pin2
  N6: Nano.A0, Rotary_Encoder.pin3, R3.Pin_1
  3V3: Nano.3V3, Si4703.3.3V, DS3231.pin3
  N7: U1.input_voltage, C1.+, D1.cathode
  N8: J1.pin1, D1.anode
  N9: Si4703_OUT.pin1, R1.Pin_0
  N10: Si4703_OUT.pin5, R4.Pin_0
  N11: PAM_INPUT.pin1, R1.Pin_1, R4.Pin_1
  N12: PAM_OUTPUT.pin1, SPEAKER.pin1
  N13: PAM_OUTPUT.pin2, SPEAKER.pin2

notes:
  +
  Eldario
  Emanuel
  versi 2
  20161128
